# Fritzing sketch SteeringDrivingPCB (saved by Fritzing 0.9.3b)

parts:
  Pico_H1 = Raspberry Pi Pico H
  S1 = H-Bridge with L298N
  DRIVING = DC Motor with two-phase hall-encoder [part_number=VT-E-G25A-06-177E]
  STEERING = DC Motor with two-phase hall-encoder [part_number=VT-E-G25A-06-177E]

nets:
  N1: Pico_H1.GND, DRIVING.pin2, STEERING.pin2
  N2: Pico_H1.3V3, STEERING.pin5
  N3: Pico_H1.GP19, DRIVING.pin4
  N4: Pico_H1.GP18, DRIVING.pin3
  N5: Pico_H1.GP17, STEERING.pin4
  N6: Pico_H1.GP16, STEERING.pin3
  N7: Pico_H1.GP15, S1.ENA
  N8: Pico_H1.GP14, S1.IN1
  N9: Pico_H1.GP13, S1.IN2
  N10: Pico_H1.GP9, S1.ENB
  N11: Pico_H1.GP8, S1.IN3
  N12: Pico_H1.GP7, S1.IN4
  N13: S1.M1-01, STEERING.pin1
  N14: S1.M1-02, STEERING.pin6
  N15: S1.M2-01, DRIVING.pin1
  N16: S1.M2-02, DRIVING.pin6

notes:
  GND
  12V+
  STEERING
  DRIVING

custom parts:
  Raspberry Pi Pico H: Raspberry Pi Pico H. Based around the RP2040 microcontroller the Pico H is a low cost microcontroller device bringing Raspberry Pi quality, cost, and easy of use to the microcontroller space.
  H-Bridge with L298N: h-bridge
